// Logisim project DATAPATH.circ as structural Verilog: 2 circuits, main circuit DataPath
module DataPath (
  input  [31:0] Input_Value,
  input  L_int_div,
  input  L_int_non_div,
  input  L_size,
  input  L_divisor,
  input  L_value,
  input  L_Index_Memory,
  input  L_Index_Input,
  input  S_Index_Memory,
  input  [1:0] S_Index_Input,
  input  CLK,
  output [23:0] size,
  output [31:0] int_non_div,
  output [31:0] int_div,
  output [23:0] Index_Memory,
  output [23:0] Index_Input,
  output [31:0] Memory_Value,
  output resto____0,
  output II____size_1
);

  wire comparator_1_eq;
  wire [23:0] Index_Input___1, int_non_div_size, multiplexer_1_out, multiplexer_2_out, size_1;
  wire [31:0] divisor, int_div_1, int_non_div_1, value___divisor;

  // Probe on int_div
  Register #(.width(32)) u_int_div (.D(int_div_1), .en(L_int_div), .Q(int_div), .clk(CLK));  // open: clr
  // Probe on int_non_div
  Register #(.width(32)) int_div_2 (.D(int_non_div_1), .en(L_int_non_div), .Q(int_non_div), .clk(CLK));  // open: clr
  // Probe on size
  Register #(.width(24)) u_size (.D(Input_Value[23:0]), .en(L_size), .Q(size), .clk(CLK));  // open: clr
  Register #(.width(32)) u_divisor (.D(Input_Value), .en(L_divisor), .Q(divisor), .clk(CLK));  // open: clr
  // Probe on divisor
  // Probe on Memory_Value
  Register #(.width(32)) value (.D(Input_Value), .en(L_value), .Q(Memory_Value), .clk(CLK));  // open: clr
  Multiplexer #(.width(24), .enable("false")) multiplexer_1 (
    .in0(int_div[23:0]), .in1(int_non_div_size), .out(multiplexer_1_out), .sel(S_Index_Memory));
  Multiplexer #(.select(2), .width(24), .enable("false")) multiplexer_2 (
    .in0(size_1), .in1(24'h1), .in2(Index_Input___1), .out(multiplexer_2_out), .sel(S_Index_Input));  // open: in3
  // Probe on Index_Memory
  Register #(.width(24)) u_Index_Memory (
    .D(multiplexer_1_out), .en(L_Index_Memory), .Q(Index_Memory), .clk(CLK));  // open: clr
  // Probe on Index_Input
  Register #(.width(24)) u_Index_Input (
    .D(multiplexer_2_out), .en(L_Index_Input), .Q(Index_Input), .clk(CLK));  // open: clr
  Adder #(.width(32)) adder_1 (.a(int_div), .b(32'h1), .out(int_div_1));  // open: cin, cout
  Adder #(.width(32)) adder_2 (.a(int_non_div), .b(32'h1), .out(int_non_div_1));  // open: cin, cout
  Adder #(.width(24)) adder_3 (.a(Index_Input), .b(24'h1), .out(Index_Input___1));  // open: cin, cout
  Adder #(.width(24)) adder_4 (.a(size), .b(int_non_div[23:0]), .out(int_non_div_size));  // open: cin, cout
  Adder #(.width(24)) adder_5 (.a(size), .b(24'h1), .out(size_1));  // open: cin, cout
  Comparator #(.width(24)) comparator_1 (.a(Index_Input), .b(size_1), .eq(comparator_1_eq));  // open: gt, lt
  Divider #(.width(32)) divider_1 (.a(Memory_Value), .b(divisor), .rem(value___divisor));  // open: out, upper
  Comparator #(.width(32)) comparator_2 (.a(value___divisor), .b({32{1'b0}}), .eq(resto____0));  // open: gt, lt
  not not_1 (II____size_1, comparator_1_eq);

  // Other names for the same wires on the sheet: value[31:0] = Memory_Value
endmodule

module ControlUnit (
  input  START,
  input  CLR,
  input  CLK,
  input  II____size_1,
  input  resto____0,
  output End,
  output Write,
  output Ls,
  output Lv,
  output Ld,
  output L_id,
  output L_ind,
  output L_IM,
  output L_II,
  output S_IM,
  output [1:0] S_II
);

  wire _1, d_ff_1_q, d_ff_6_q, d_ff_11_q, d_ff_12_q, d_ff_13_q, demultiplexer_1_out0, demultiplexer_2_out1,
       L_II0, Lv0, Lv1, or_1_out, RESET, START_t, Write0, Write1;

  D_Flip_Flop d_ff_1 (.clk(CLK), .D(demultiplexer_1_out0), .Q(d_ff_1_q), .preset(RESET));  // open: Qn, en, reset
  Demultiplexer #(.enable("false")) demultiplexer_1 (
    .out0(demultiplexer_1_out0), .out1(Ls), .in(d_ff_1_q), .sel(START_t));
  D_Flip_Flop d_ff_2 (.clk(CLK), .D(S_II[0]), .Q(Lv0), .reset(RESET));  // open: Qn, preset, en
  D_Flip_Flop d_ff_3 (.clk(CLK), .D(S_IM), .Q(Write1), .reset(RESET));  // open: Qn, preset, en
  D_Flip_Flop d_ff_4 (.clk(CLK), .D(_1), .Q(Write0), .reset(RESET));  // open: Qn, preset, en
  D_Flip_Flop d_ff_5 (.Q(START_t), .preset(START), .reset(CLR));  // open: clk, D, Qn, en
  xor xor_1 (RESET, START_t, d_ff_6_q);
  D_Flip_Flop d_ff_6 (.clk(CLK), .D(START_t), .Q(d_ff_6_q));  // open: Qn, preset, en, reset
  D_Flip_Flop d_ff_7 (.clk(CLK), .D(Ls), .Q(L_II0), .reset(RESET));  // open: Qn, preset, en
  or or_1 (or_1_out, Lv0, Lv1);
  D_Flip_Flop d_ff_8 (.clk(CLK), .D(Write1), .Q(L_ind), .reset(RESET));  // open: Qn, preset, en
  D_Flip_Flop d_ff_9 (.clk(CLK), .D(Write0), .Q(L_id), .reset(RESET));  // open: Qn, preset, en
  D_Flip_Flop d_ff_10 (.clk(CLK), .D(L_II0), .Q(Ld), .reset(RESET));  // open: Qn, preset, en
  D_Flip_Flop d_ff_11 (.clk(CLK), .D(or_1_out), .Q(d_ff_11_q), .reset(RESET));  // open: Qn, preset, en
  D_Flip_Flop d_ff_12 (.clk(CLK), .D(L_ind), .Q(d_ff_12_q), .reset(RESET));  // open: Qn, preset, en
  D_Flip_Flop d_ff_13 (.clk(CLK), .D(L_id), .Q(d_ff_13_q), .reset(RESET));  // open: Qn, preset, en
  Demultiplexer #(.enable("false")) demultiplexer_2 (
    .out0(End), .out1(demultiplexer_2_out1), .in(d_ff_11_q), .sel(II____size_1));
  D_Flip_Flop d_ff_14 (.clk(CLK), .D(Ld), .Q(S_II[0]), .reset(RESET));  // open: Qn, preset, en
  or or_2 (S_II[1], d_ff_12_q, d_ff_13_q);
  or or_3 (Write, Write0, Write1);
  or or_4 (Lv, Lv0, Lv1);
  or or_5 (L_IM, S_IM, _1);
  or or_6 (L_II, L_II0, S_II[0], S_II[1]);
  Demultiplexer #(.enable("false")) demultiplexer_3 (
    .out0(S_IM), .out1(_1), .in(demultiplexer_2_out1), .sel(resto____0));
  D_Flip_Flop d_ff_15 (.clk(CLK), .D(S_II[1]), .Q(Lv1), .reset(RESET));  // open: Qn, preset, en

  // Other names for the same wires on the sheet: L_IM0 = _1; _0 = S_IM; L_IM1 = S_IM; L_II1 = S_II[0];
  //   L_II2 = S_II[1]
endmodule
