// Logisim project DATAPATH.circ as structural Verilog: 2 circuits, main circuit DataPath
module DataPath (
  input  [31:0] N_in,
  input  La,
  input  Lb,
  input  Sa,
  input  Sb,
  input  CLK,
  output b____0,
  output [31:0] N_Out
);

  wire comparator_1_eq;
  wire [31:0] a_6, b, b_1, multiplexer_1_out, multiplexer_2_out;

  Multiplexer #(.width(32), .enable("false")) multiplexer_1 (.in0(N_in), .in1(b_1), .out(multiplexer_1_out), .sel(Sb));
  Subtractor #(.width(32)) subtractor_1 (.a(b), .b(32'h1), .out(b_1));  // open: bin, bout
  Multiplier #(.width(32)) multiplier_1 (.a(N_Out), .b(32'h6), .out(a_6));  // open: cin, cout
  // Probe on b
  Register #(.width(32)) u_b (.D(multiplexer_1_out), .en(Lb), .Q(b), .clk(CLK));  // open: clr
  Comparator #(.width(32)) comparator_1 (.a(b), .b({32{1'b0}}), .eq(comparator_1_eq));  // open: gt, lt
  not not_1 (b____0, comparator_1_eq);
  Multiplexer #(.width(32), .enable("false")) multiplexer_2 (.in0(32'h6), .in1(a_6), .out(multiplexer_2_out), .sel(Sa));
  // Probe on N_Out
  Register #(.width(32)) a (.D(multiplexer_2_out), .en(La), .Q(N_Out), .clk(CLK));  // open: clr

  // Other names for the same wires on the sheet: a[31:0] = N_Out; n[31:0] = N_in
endmodule

module ControlUnit (
  input  START,
  input  b____0,
  input  CLK,
  output END,
  output La,
  output Lb,
  output Sa,
  output Sb
);

  wire d_ff_1_q, d_ff_2_q, demultiplexer_1_out0, La0, Lb0, or_1_out, RESET, WHILE_q;

  D_Flip_Flop d_ff_1 (.clk(CLK), .D(START), .Q(d_ff_1_q));  // open: Qn, preset, en, reset
  Demultiplexer #(.enable("false")) demultiplexer_1 (
    .out0(demultiplexer_1_out0), .out1(Lb0), .in(d_ff_2_q), .sel(START));
  D_Flip_Flop d_ff_2 (.clk(CLK), .D(demultiplexer_1_out0), .Q(d_ff_2_q), .preset(RESET));  // open: Qn, en, reset
  xor xor_1 (RESET, START, d_ff_1_q);
  D_Flip_Flop d_ff_3 (.clk(CLK), .D(Lb0), .Q(La0), .reset(RESET));  // open: Qn, preset, en
  or or_1 (or_1_out, La0, Sa);
  or or_2 (La, La0, Sa);
  or or_3 (Lb, Lb0, La0, Sa);
  or or_4 (Sb, La0, Sa);
  D_Flip_Flop WHILE (.clk(CLK), .D(or_1_out), .Q(WHILE_q), .reset(RESET));  // open: Qn, preset, en
  Demultiplexer #(.enable("false")) demultiplexer_2 (.out0(END), .out1(Sa), .in(WHILE_q), .sel(b____0));

  // Other names for the same wires on the sheet: Lb1 = La0; Sb0 = La0; La1 = Sa; Lb2 = Sa; Sb1 = Sa
endmodule
