// Logisim project DATAPATH.circ as structural Verilog: 2 circuits, main circuit DataPath
module DataPath (
  input  [31:0] x1,
  input  [31:0] x2,
  input  [31:0] x3,
  input  [31:0] x4,
  input  [31:0] y1,
  input  [31:0] y2,
  input  [31:0] y3,
  input  CLK,
  input  LY1,
  input  SX20,
  input  SY2,
  input  LX1,
  input  LY2,
  input  SX21,
  input  SY4,
  input  LX2,
  input  LY3,
  input  SX40,
  input  [31:0] y4,
  input  ST,
  input  LX3,
  input  LY4,
  input  SX41,
  input  LX4,
  input  LT,
  output T,
  output X2__0,
  output X4__0,
  output X4__X2
);

  wire [31:0] multiplexer_1_out, multiplexer_2_out, multiplexer_3_out, multiplexer_4_out, X1_t, X2_t, X2_X1,
       X2_Y4, X3_t, X4_t, X4_X3, X4_Y2, Y1_t, Y2_t, Y2_Y1, Y3_t, Y4_t, Y4_Y3;

  // Probe on X4_X3
  Multiplexer #(.select(2), .width(32), .enable("false")) multiplexer_1 (
    .in0(x2), .in1(X2_X1), .in2(X2_Y4), .out(multiplexer_1_out), .sel({SX21, SX20}));  // open: in3
  Multiplexer #(.select(2), .width(32), .enable("false")) multiplexer_2 (
    .in0(x4), .in1(X4_X3), .in2(X4_Y2), .out(multiplexer_2_out), .sel({SX41, SX40}));  // open: in3
  // Probe on X1_t
  Register #(.width(32)) u_X1 (.D(x1), .en(LX1), .Q(X1_t), .clk(CLK));  // open: clr
  // Probe on X2_t
  Register #(.width(32)) u_X2 (.D(multiplexer_1_out), .en(LX2), .Q(X2_t), .clk(CLK));  // open: clr
  // Probe on X3_t
  Register #(.width(32)) u_X3 (.D(x3), .en(LX3), .Q(X3_t), .clk(CLK));  // open: clr
  // Probe on X4_t
  Register #(.width(32)) u_X4 (.D(multiplexer_2_out), .en(LX4), .Q(X4_t), .clk(CLK));  // open: clr
  Multiplexer #(.width(32), .enable("false")) multiplexer_3 (.in0(y2), .in1(Y2_Y1), .out(multiplexer_3_out), .sel(SY2));
  Multiplexer #(.width(32), .enable("false")) multiplexer_4 (.in0(y4), .in1(Y4_Y3), .out(multiplexer_4_out), .sel(SY2));
  // Probe on Y1_t
  Register #(.width(32)) u_Y1 (.D(y1), .en(LY1), .Q(Y1_t), .clk(CLK));  // open: clr
  // Probe on Y2_t
  Register #(.width(32)) u_Y2 (.D(multiplexer_3_out), .en(LY2), .Q(Y2_t), .clk(CLK));  // open: clr
  // Probe on Y3_t
  Register #(.width(32)) u_Y3 (.D(y3), .en(LY3), .Q(Y3_t), .clk(CLK));  // open: clr
  // Probe on Y4_t
  Register #(.width(32)) u_Y4 (.D(multiplexer_4_out), .en(LY4), .Q(Y4_t), .clk(CLK));  // open: clr
  // Probe on T
  Register #(.width(1)) Y2_2 (.D(ST), .en(LT), .Q(T), .clk(CLK));  // open: clr
  Comparator #(.width(32)) comparator_1 (.a(X2_t), .b({32{1'b0}}), .eq(X2__0));  // open: gt, lt
  Comparator #(.width(32)) comparator_2 (.a(X4_t), .b({32{1'b0}}), .eq(X4__0));  // open: gt, lt
  Comparator #(.width(32)) comparator_3 (.a(X4_t), .b(X2_t), .eq(X4__X2));  // open: gt, lt
  Subtractor #(.width(32)) subtractor_1 (.a(X2_t), .b(X1_t), .out(X2_X1));  // open: bin, bout
  Subtractor #(.width(32)) subtractor_2 (.a(X4_t), .b(X3_t), .out(X4_X3));  // open: bin, bout
  Subtractor #(.width(32)) subtractor_3 (.a(Y2_t), .b(Y1_t), .out(Y2_Y1));  // open: bin, bout
  Subtractor #(.width(32)) subtractor_4 (.a(Y4_t), .b(Y3_t), .out(Y4_Y3));  // open: bin, bout
  Multiplier #(.width(32)) multiplier_1 (.a(X2_t), .b(Y4_t), .out(X2_Y4));  // open: cin, cout
  Multiplier #(.width(32)) multiplier_2 (.a(X4_t), .b(Y2_t), .out(X4_Y2));  // open: cin, cout
  // Probe on X4_X3
endmodule

module ControlUnit (
  input  START,
  input  CLK,
  input  X2__0,
  input  X4__0,
  input  X2__X4,
  output END,
  output LT,
  output LX1,
  output SX20,
  output LX2,
  output LX3,
  output SX21,
  output SX40,
  output LX4,
  output SX41,
  output LY1,
  output SY2,
  output LY2,
  output SY4,
  output LY3,
  output ST,
  output LY4
);

  wire _1, _2, COND, d_ff_1_q, d_ff_3_q, d_ff_14_q, demultiplexer_2_out0, LT1, LX20, LX40, LY20, LY40,
       or_1_out, or_2_out, RESET;

  or or_1 (or_1_out, _1, _2);
  Demultiplexer #(.enable("false")) demultiplexer_1 (.out0(ST), .out1(LT1), .in(or_1_out), .sel(X2__X4));
  D_Flip_Flop d_ff_1 (.clk(CLK), .D(demultiplexer_2_out0), .Q(d_ff_1_q), .preset(RESET));  // open: Qn, en, reset
  Demultiplexer #(.enable("false")) demultiplexer_2 (
    .out0(demultiplexer_2_out0), .out1(LX1), .in(d_ff_1_q), .sel(START));
  D_Flip_Flop d_ff_2 (.clk(CLK), .D(LX3), .Q(LY3), .reset(RESET));  // open: Qn, preset, en
  D_Flip_Flop d_ff_3 (.clk(CLK), .D(START), .Q(d_ff_3_q));  // open: Qn, preset, en, reset
  D_Flip_Flop d_ff_4 (.clk(CLK), .D(LY3), .Q(LX40), .reset(RESET));  // open: Qn, preset, en
  xor xor_1 (RESET, START, d_ff_3_q);
  D_Flip_Flop d_ff_5 (.clk(CLK), .D(SY2), .Q(SX21), .reset(RESET));  // open: Qn, preset, en
  or or_2 (or_2_out, ST, LT1);
  D_Flip_Flop d_ff_6 (.clk(CLK), .D(LX1), .Q(LY1), .reset(RESET));  // open: Qn, preset, en
  D_Flip_Flop d_ff_7 (.clk(CLK), .D(LX40), .Q(LY40), .reset(RESET));  // open: Qn, preset, en
  D_Flip_Flop d_ff_8 (.clk(CLK), .D(or_2_out), .Q(END), .reset(RESET));  // open: Qn, preset, en
  D_Flip_Flop d_ff_9 (.clk(CLK), .D(LY1), .Q(LX20), .reset(RESET));  // open: Qn, preset, en
  D_Flip_Flop d_ff_10 (.clk(CLK), .D(LY40), .Q(SX20), .reset(RESET));  // open: Qn, preset, en
  or or_3 (LT, ST, LT1);
  or or_4 (LX2, LX20, SX21, SX20);
  or or_5 (LX4, LX40, SX21, SX20);
  or or_6 (LY2, LY20, SY2);
  or or_7 (LY4, LY40, SY2);
  D_Flip_Flop d_ff_11 (.clk(CLK), .D(LX20), .Q(LY20), .reset(RESET));  // open: Qn, preset, en
  D_Flip_Flop d_ff_12 (.clk(CLK), .D(SX21), .Q(_2), .reset(RESET));  // open: Qn, preset, en
  D_Flip_Flop d_ff_13 (.clk(CLK), .D(LY20), .Q(LX3), .reset(RESET));  // open: Qn, preset, en
  Demultiplexer #(.enable("false")) demultiplexer_3 (.out0(SY2), .out1(_1), .in(d_ff_14_q), .sel(COND));
  D_Flip_Flop d_ff_14 (.clk(CLK), .D(SX20), .Q(d_ff_14_q), .reset(RESET));  // open: Qn, preset, en
  or or_8 (COND, X2__0, X4__0);

  assign SX40 = SX20;
  assign SX41 = SX21;
  assign SY4 = SY2;

  // Other names for the same wires on the sheet: LT0 = ST; LX2_t = SX21; LX4_t = SX21; LX21 = SX20; LX41 = SX20;
  //   _0 = SY2; LY21 = SY2; LY41 = SY2

  // Notes on the sheet:
  //   ENTRADAS
  //   SALIDAS
endmodule
